// Logisim project knp4.circ as structural Verilog: 1 circuit, main circuit main
// 0x6
module main (
  input  I,
  input  PC,
  input  DR,
  input  AC,
  input  in_5,
  input  TR,
  input  in_7,
  input  in_8,
  output [15:0] out_9,
  output [3:0] out_10
);

  wire and_1_out, and_2_out, and_3_out, and_4_out, and_5_out, and_6_out, clock_1_out, decoder_1_out11,
       decoder_2_out0, decoder_2_out1, decoder_2_out2, decoder_2_out3, decoder_2_out4, decoder_2_out5,
       decoder_2_out6, decoder_2_out7, decoder_3_out1, decoder_3_out2, decoder_3_out3, decoder_3_out4,
       decoder_3_out5, decoder_3_out6, not_1_out, not_2_out, or_1_out, or_5_out, or_6_out, or_7_out,
       register_7_q;
  wire [2:0] counter_1_q, or_2_out;
  wire [11:0] bit_extender_1_out, bit_extender_2_out, register_1_q, register_2_q;
  wire [15:0] bit_extender_3_out, bit_extender_4_out, bit_extender_5_out, ram_1_data, register_3_q,
       register_4_q, register_5_q, register_6_q;

  Clock clock_1 (.out(clock_1_out));
  Bit_Extender #(.in_width(16), .out_width(12)) bit_extender_1 (.in(out_9), .out(bit_extender_1_out));
  Bit_Extender #(.in_width(16), .out_width(12)) bit_extender_2 (.in(out_9), .out(bit_extender_2_out));
  Register #(.width(12)) register_1 (
    .D(bit_extender_1_out), .en(or_1_out), .Q(register_1_q), .clk(clock_1_out), .clr(and_1_out));
  Register #(.width(12)) register_2 (
    .D(bit_extender_2_out), .en(PC), .Q(register_2_q), .clk(clock_1_out));  // open: clr
  Register #(.width(16)) register_3 (.D(out_9), .en(DR), .Q(register_3_q), .clk(clock_1_out));  // open: clr
  Register #(.width(16)) register_4 (.D(out_9), .en(AC), .Q(register_4_q), .clk(clock_1_out), .clr(decoder_1_out11));
  Register #(.width(16)) register_5 (.D(out_9), .en(decoder_3_out2), .Q(register_5_q), .clk(clock_1_out));  // open: clr
  Register #(.width(16)) register_6 (.D(out_9), .en(TR), .Q(register_6_q), .clk(clock_1_out));  // open: clr
  assign bit_extender_3_out = {{4{1'b0}}, register_1_q};  // Bit_Extender bit_extender_3
  assign bit_extender_4_out = {{4{1'b0}}, register_2_q};  // Bit_Extender bit_extender_4
  RAM #(.addrWidth(12), .dataWidth(16), .bus("separate")) ram_1 (
    .addr(register_1_q), .din(out_9), .data(ram_1_data), .str(and_6_out), .sel(in_7), .clk(clock_1_out),
    .ld(or_5_out));  // open: clr
  or or_1 (or_1_out, or_6_out, and_4_out);
  Multiplexer #(.select(3), .width(16)) multiplexer_1 (
    .in1(bit_extender_3_out), .in2(bit_extender_4_out), .in3(register_3_q), .in4(register_4_q),
    .in5(bit_extender_5_out), .in6(register_6_q), .in7(ram_1_data), .out(out_9), .sel(or_2_out), .en(in_5));  // open: in0
  Decoder #(.select(4)) decoder_1 (
    .out11(decoder_1_out11), .sel(out_10), .en(and_2_out));  // open: out0, out1, out2, out3, out4, out5, out6, out7, out8, out9, out10, out12, out13, out14, out15
  Counter #(.width(3), .max('h6)) counter_1 (.Q(counter_1_q), .clk(clock_1_out));  // open: load, D, count, carry, clr
  assign bit_extender_5_out = {{4{1'b0}}, register_5_q[11:0]};  // Bit_Extender bit_extender_5
  or or_2 (or_2_out[0], and_4_out, decoder_3_out3, decoder_3_out2, and_3_out);
  or or_3 (or_2_out[1], decoder_3_out2, and_4_out, decoder_3_out1);
  or or_4 (or_2_out[2], and_5_out, decoder_3_out3, decoder_3_out2, and_4_out);
  or or_5 (or_5_out, decoder_3_out2, and_4_out);
  BitFinder #(.width(16)) bitfinder_1 (.in(out_9), .index(out_10));  // open: found
  and and_1 (and_1_out, decoder_3_out6, decoder_2_out3);
  Decoder #(.select(3)) decoder_2 (
    .out0(decoder_2_out0), .out1(decoder_2_out1), .out2(decoder_2_out2), .out3(decoder_2_out3),
    .out4(decoder_2_out4), .out5(decoder_2_out5), .out6(decoder_2_out6), .out7(decoder_2_out7),
    .sel(register_5_q[14:12]), .en(I));
  Register #(.width(1)) register_7 (.D(register_5_q[15]), .Q(register_7_q), .clk(clock_1_out));  // open: en, clr
  and and_2 (and_2_out, not_1_out, decoder_2_out7, decoder_3_out4);
  not not_1 (not_1_out, register_7_q);
  and and_3 (and_3_out, decoder_2_out7, decoder_3_out4);
  and and_4 (and_4_out, register_7_q, not_2_out, decoder_3_out4);
  Decoder #(.select(3)) decoder_3 (
    .out1(decoder_3_out1), .out2(decoder_3_out2), .out3(decoder_3_out3), .out4(decoder_3_out4),
    .out5(decoder_3_out5), .out6(decoder_3_out6), .sel(counter_1_q), .en(in_8));  // open: out0, out7
  or or_6 (or_6_out, decoder_3_out3, decoder_3_out1);
  or or_7 (or_7_out, decoder_2_out3, decoder_2_out5);
  and and_5 (and_5_out, decoder_2_out3, decoder_3_out5);
  not not_2 (not_2_out, decoder_2_out7);
  and and_6 (and_6_out, decoder_3_out5, or_7_out);

  // Notes on the sheet:
  //   AR
  //   IR
  //   (for register reference instruction)
  //   BUS
  //   T3
  //   T2
  //   T1
  //   T0
  //   T4
  //   T5
endmodule
